# Fritzing sketch secu (saved by Fritzing 0.9.3b)
breadboards: 1

parts:
  Raspberry_Pi_1 = Raspberry Pi 3 [part_number=RPI-3-V1.2]
  R1 = Resistor [tolerance=±5% resistance=330 package="0603 [SMD]"]
  R2 = Resistor [tolerance=±5% resistance=330 package="0603 [SMD]"]
  LED2 = LED - 3mm [color="Blue (430nm)" package="3 mm [THT]"]
  LED3 = LED - 3mm [color="Red (633nm)" package="3 mm [THT]"]
  R3 = Resistor [tolerance=±5% resistance=1k package=THT]
  R4 = Resistor [tolerance=±5% resistance=1k package=THT]
  R5 = Resistor [tolerance=±5% resistance=1k package=THT]
  R6 = Resistor [tolerance=±5% resistance=1k package=THT]
  R7 = Resistor [tolerance=±5% resistance=1k package=THT]
  R8 = Resistor [tolerance=±5% resistance=1k package=THT]
  J1 = Piezo Speaker
  Q2 = TRANSISTOR_NPN [package=to-92]
  R9 = Resistor [tolerance=±5% resistance=1k package=THT]

nets:
  N1: Raspberry_Pi_1.GIPO4, LED3.anode
  N2: Raspberry_Pi_1.GIPO17, LED2.anode
  N3: Raspberry_Pi_1.GIPO27, Raspberry_Pi_1.GIPO22, R3.Pin_0, R4.Pin_0, R5.Pin_0, R6.Pin_0, R7.Pin_0, R8.Pin_0
  N4: Raspberry_Pi_1.GIPO5, R5.Pin_1
  N5: Raspberry_Pi_1.GIPO6, R6.Pin_1
  N6: Raspberry_Pi_1.GIPO13, R7.Pin_1
  N7: Raspberry_Pi_1.GIPO21, R9.Pin_1
  N8: Raspberry_Pi_1.GIPO20, R8.Pin_1
  N9: Raspberry_Pi_1.GIPO8, Raspberry_Pi_1.GIPO25, R4.Pin_1
  N10: Raspberry_Pi_1.GIPO24, Raspberry_Pi_1.GIPO23, R3.Pin_1
  N11: Raspberry_Pi_1.GIPO14, Raspberry_Pi_1.GND, R1.Pin_0, R2.Pin_0, Q2.C
  N12: Raspberry_Pi_1.5V, J1.pin2
  N13: R1.Pin_1, LED3.cathode
  N14: R2.Pin_1, LED2.cathode
  N15: J1.pin1, Q2.E
  N16: Q2.B, R9.Pin_0
